// Logisim project CPU.circ as structural Verilog: 7 circuits, main circuit main
module main (
  input  RESET
);

  wire clock_1_out, cpu_1_clock_ou, cpu_1_read, cpu_1_wrt, xor_1_out;
  wire [15:0] cpu_1_addr, cpu_1_instruction_pointer, cpu_1_op, MEMORY_dout, PROGRAM_dout;

  Clock clock_1 (.out(clock_1_out));
  RAM #(.addrWidth(16), .dataWidth(16), .trigger("falling")) PROGRAM (
    .addr(cpu_1_instruction_pointer), .clk(xor_1_out), .dout(PROGRAM_dout));  // open: we, oe, din
  xor xor_1 (xor_1_out, clock_1_out, RESET);
  CPU cpu_1 (
    .INSTRUCTION(PROGRAM_dout), .Clock(xor_1_out), .Reset(RESET), .IP(MEMORY_dout),
    .Instruction_Pointer(cpu_1_instruction_pointer), .ADDR(cpu_1_addr), .WRT(cpu_1_wrt), .READ(cpu_1_read),
    .Clock_OU(cpu_1_clock_ou), .OP(cpu_1_op));
  RAM #(.addrWidth(16), .asyncread("true"), .clearpin("true"), .dataWidth(16)) MEMORY (
    .addr(cpu_1_addr), .we(cpu_1_wrt), .oe(cpu_1_read), .clk(cpu_1_clock_ou), .din(cpu_1_op),
    .dout(MEMORY_dout), .clr(RESET));
endmodule

module CPU (
  input  [15:0] INSTRUCTION,
  input  Clock,
  input  Reset,
  input  [15:0] IP,
  output [15:0] Instruction_Pointer,
  output [15:0] ADDR,
  output WRT,
  output READ,
  output Clock_OU,
  output [15:0] OP
);

  wire A1, A2, ADD, AMD, and_4_out, and_5_out, and_6_out, AS, B1, B2, BP1, BP2, BPS, BS, buffer_1_out,
       buffer_2_out, buffering_3_out_2, buffering_4_out_2, C1, C2, CLOCK1, CLOCK2, CLOCK3, CMP,
       controlled_buffer_6_out, controlled_buffer_9_out, controlled_buffer_10_out, controlled_buffer_39_out,
       cpu_decoder_1_noop, cpu_decoder_1_ou, cpu_decoder_1_src_1, cpu_decoder_1_src_2, CS, D1, D2, DS, E1,
       E2, ES, F1, F2, FS, imm_save2_1_opcode_disable, imm_save2_1_src1_imm, imm_save2_1_src2_imm, IN_DIS,
       INV_VAL, JE, JG, JL, JMP, MOV, not_1_out, not_2_out, not_3_out, not_4_out, not_5_out, not_6_out,
       not_7_out, or_4_out, or_5_out, OW, POP, PSHPOP, PUSH, SHL, SHR, SP1, SP2, SPS, SUB, WRT_t, xor_2_out,
       XOW;
  wire [2:0] comparator_1_gt, register_1_q;
  wire [15:0] A_q, adder_1_out, and_1_out, B_q, BP_q, C_q, controlled_buffer_2_out, controlled_buffer_8_out,
       controlled_buffer_12_out, controlled_buffer_13_out, D_q, E_q, F_q, imm_save2_1_instruction,
       imm_save2_1_src1, imm_save2_1_src2, or_2_out, shifter_1_out, shifter_2_out, SP_q, SRC2_IMM,
       subtractor_1_out, subtractor_2_out, xor_1_out;

  Controlled_Buffer #(.width(16)) controlled_buffer_1 ();  // open: in, out, en
  Buffering buffering_1 (.in_1(Clock), .out_2(CLOCK1));
  not not_1 (not_1_out, IN_DIS);
  assign {controlled_buffer_2_out[15:14], INV_VAL, controlled_buffer_2_out[12:0]} = not_1_out ? INSTRUCTION : 16'bz;  // Controlled_Buffer controlled_buffer_2
  assign {controlled_buffer_2_out[15:14], INV_VAL, controlled_buffer_2_out[12:0]} = IN_DIS ? imm_save2_1_instruction : 16'bz;  // Controlled_Buffer controlled_buffer_3
  IMM_SAVE2 imm_save2_1 (
    .IMM_VALS(controlled_buffer_2_out[15:14]), .INSTR_IN(INSTRUCTION), .Clock(Clock), .Reset(Reset),
    .INSTRUCTION(imm_save2_1_instruction), .OPCODE_DISABLE(imm_save2_1_opcode_disable),
    .SRC1_IMM(imm_save2_1_src1_imm), .SRC1(imm_save2_1_src1), .SRC2_IMM(imm_save2_1_src2_imm),
    .SRC2(imm_save2_1_src2));
  or or_1 (IN_DIS, imm_save2_1_src2_imm, imm_save2_1_src1_imm);
  Buffering buffering_2 (.in_1(CLOCK2), .out_2(CLOCK3));
  not not_2 (not_2_out, imm_save2_1_src1_imm);
  assign OP = imm_save2_1_src1_imm ? imm_save2_1_src1 : 16'bz;  // Controlled_Buffer controlled_buffer_4
  not not_3 (not_3_out, imm_save2_1_src2_imm);
  assign SRC2_IMM = imm_save2_1_src2_imm ? imm_save2_1_src2 : 16'bz;  // Controlled_Buffer controlled_buffer_5
  not not_4 (not_4_out, READ);
  assign controlled_buffer_6_out = not_4_out ? CLOCK2 : 1'bz;  // Controlled_Buffer controlled_buffer_6
  CPU_Decoder cpu_decoder_1 (
    .OPCODE(controlled_buffer_2_out[12:9]), .UNENABLE(imm_save2_1_opcode_disable), .NOOP(cpu_decoder_1_noop),
    .MOV(MOV), .AMD(AMD), .OW(OW), .XOW(XOW), .ADD(ADD), .SUB(SUB), .SHL(SHL), .SHR(SHR), .CMP(CMP),
    .JMP(JMP), .JE(JE), .JL(JL), .JG(JG), .WRT(WRT_t), .READ(READ), .SRC_1(cpu_decoder_1_src_1),
    .SRC_2(cpu_decoder_1_src_2), .OU(cpu_decoder_1_ou));
  assign controlled_buffer_6_out = READ ? buffering_3_out_2 : 1'bz;  // Controlled_Buffer controlled_buffer_7
  Buffering buffering_3 (.in_1(CLOCK3), .out_2(buffering_3_out_2));
  assign controlled_buffer_8_out = READ ? IP : 16'bz;  // Controlled_Buffer controlled_buffer_8
  not not_5 (not_5_out, READ);
  assign controlled_buffer_9_out = not_2_out ? cpu_decoder_1_src_1 : 1'bz;  // Controlled_Buffer controlled_buffer_9
  assign controlled_buffer_10_out = not_3_out ? cpu_decoder_1_src_2 : 1'bz;  // Controlled_Buffer controlled_buffer_10
  assign controlled_buffer_8_out = not_5_out ? controlled_buffer_12_out : 16'bz;  // Controlled_Buffer controlled_buffer_11
  assign controlled_buffer_12_out = not_6_out ? controlled_buffer_13_out : 16'bz;  // Controlled_Buffer controlled_buffer_12
  not not_6 (not_6_out, INV_VAL);
  assign controlled_buffer_12_out = INV_VAL ? ~controlled_buffer_13_out : 16'bz;  // Controlled_Inverter controlled_inverter_1
  Register #(.width(16)) A (.D(controlled_buffer_8_out), .en(AS), .clk(controlled_buffer_6_out), .Q(A_q), .clr(Reset));
  Register #(.width(16)) B (.D(controlled_buffer_8_out), .en(BS), .clk(controlled_buffer_6_out), .Q(B_q), .clr(Reset));
  Register #(.width(16)) C (.D(controlled_buffer_8_out), .en(CS), .clk(controlled_buffer_6_out), .Q(C_q), .clr(Reset));
  Register #(.width(16)) D (.D(controlled_buffer_8_out), .en(DS), .clk(controlled_buffer_6_out), .Q(D_q), .clr(Reset));
  Register #(.width(16)) E (.D(controlled_buffer_8_out), .en(ES), .clk(controlled_buffer_6_out), .Q(E_q), .clr(Reset));
  Register #(.width(16)) F (.D(controlled_buffer_8_out), .en(FS), .clk(controlled_buffer_6_out), .Q(F_q), .clr(Reset));
  Register #(.width(16)) BP (
    .D(controlled_buffer_8_out), .en(BPS), .clk(controlled_buffer_6_out), .Q(BP_q), .clr(Reset));
  Counter #(.max('hffff), .width(16)) SP (
    .clr(Reset), .load(SPS), .up(WRT_t), .count(PSHPOP), .clk(controlled_buffer_6_out),
    .D(controlled_buffer_8_out), .Q(SP_q));  // open: carry
  Buffering buffering_4 (.in_1(CLOCK1), .out_2(buffering_4_out_2));
  assign controlled_buffer_13_out = MOV ? OP : 16'bz;  // Controlled_Buffer controlled_buffer_13
  assign controlled_buffer_13_out = AMD ? and_1_out : 16'bz;  // Controlled_Buffer controlled_buffer_14
  assign controlled_buffer_13_out = OW ? or_2_out : 16'bz;  // Controlled_Buffer controlled_buffer_15
  assign controlled_buffer_13_out = XOW ? xor_1_out : 16'bz;  // Controlled_Buffer controlled_buffer_16
  assign controlled_buffer_13_out = SHL ? shifter_1_out : 16'bz;  // Controlled_Buffer controlled_buffer_17
  assign controlled_buffer_13_out = SHR ? shifter_2_out : 16'bz;  // Controlled_Buffer controlled_buffer_18
  assign controlled_buffer_13_out = ADD ? adder_1_out : 16'bz;  // Controlled_Buffer controlled_buffer_19
  assign controlled_buffer_13_out = SUB ? subtractor_2_out : 16'bz;  // Controlled_Buffer controlled_buffer_20
  assign OP = A1 ? A_q : 16'bz;  // Controlled_Buffer controlled_buffer_21
  assign SRC2_IMM = A2 ? A_q : 16'bz;  // Controlled_Buffer controlled_buffer_22
  assign OP = B1 ? B_q : 16'bz;  // Controlled_Buffer controlled_buffer_23
  assign SRC2_IMM = B2 ? B_q : 16'bz;  // Controlled_Buffer controlled_buffer_24
  assign OP = C1 ? C_q : 16'bz;  // Controlled_Buffer controlled_buffer_25
  assign SRC2_IMM = C2 ? C_q : 16'bz;  // Controlled_Buffer controlled_buffer_26
  assign OP = D1 ? D_q : 16'bz;  // Controlled_Buffer controlled_buffer_27
  assign SRC2_IMM = D2 ? D_q : 16'bz;  // Controlled_Buffer controlled_buffer_28
  assign OP = E1 ? E_q : 16'bz;  // Controlled_Buffer controlled_buffer_29
  assign SRC2_IMM = E2 ? E_q : 16'bz;  // Controlled_Buffer controlled_buffer_30
  assign OP = F1 ? F_q : 16'bz;  // Controlled_Buffer controlled_buffer_31
  assign SRC2_IMM = F2 ? F_q : 16'bz;  // Controlled_Buffer controlled_buffer_32
  assign OP = BP1 ? BP_q : 16'bz;  // Controlled_Buffer controlled_buffer_33
  assign SRC2_IMM = BP2 ? BP_q : 16'bz;  // Controlled_Buffer controlled_buffer_34
  assign and_1_out = OP & SRC2_IMM;  // AND_Gate and_1, 16 bits wide
  assign or_2_out = OP | SRC2_IMM;  // OR_Gate or_2, 16 bits wide
  assign xor_1_out = OP ^ SRC2_IMM;  // XOR_Gate xor_1, 16 bits wide
  assign OP = SP1 ? SP_q : 16'bz;  // Controlled_Buffer controlled_buffer_35
  assign SRC2_IMM = SP2 ? SP_q : 16'bz;  // Controlled_Buffer controlled_buffer_36
  Buffering buffering_5 (.in_1(buffering_4_out_2), .out_2(CLOCK2));
  REG_Decoder reg_decoder_1 (
    .IP(controlled_buffer_2_out[8:6]), .ENABLE(controlled_buffer_9_out), .A(A1), .B(B1), .C(C1), .D(D1),
    .s(E1), .t(F1), .BP(BP1), .SP(SP1));
  REG_Decoder reg_decoder_2 (
    .IP(controlled_buffer_2_out[5:3]), .ENABLE(controlled_buffer_10_out), .A(A2), .B(B2), .C(C2), .D(D2),
    .s(E2), .t(F2), .BP(BP2), .SP(SP2));
  REG_Decoder reg_decoder_3 (
    .IP(controlled_buffer_2_out[2:0]), .ENABLE(cpu_decoder_1_ou), .A(AS), .B(BS), .C(CS), .D(DS), .s(ES),
    .t(FS), .BP(BPS), .SP(SPS));
  Subtractor #(.width(16)) subtractor_1 (.a(SP_q), .b({16{1'b0}}), .out(subtractor_1_out), .bin(POP));  // open: bout
  Subtractor #(.width(16)) subtractor_2 (.a(OP), .b(SRC2_IMM), .out(subtractor_2_out));  // open: bin, bout
  not not_7 (not_7_out, PSHPOP);
  assign ADDR = PSHPOP ? subtractor_1_out : 16'bz;  // Controlled_Buffer controlled_buffer_37
  Shifter #(.width(16)) shifter_1 (.in(OP), .\dist (4'b0001), .out(shifter_1_out));
  Shifter #(.shift("lr"), .width(16)) shifter_2 (.in(OP), .\dist (4'b0001), .out(shifter_2_out));
  Adder #(.width(16)) adder_1 (.a(OP), .b(SRC2_IMM), .out(adder_1_out));  // open: cin, cout
  and and_2 (PUSH, WRT_t, INV_VAL);
  and and_3 (POP, READ, INV_VAL);
  assign ADDR = not_7_out ? SRC2_IMM : 16'bz;  // Controlled_Buffer controlled_buffer_38
  Comparator #(.mode("unsigned"), .width(16)) comparator_1 (
    .a(OP), .b(SRC2_IMM), .gt(comparator_1_gt[0]), .eq(comparator_1_gt[1]), .lt(comparator_1_gt[2]));
  or or_3 (PSHPOP, PUSH, POP);
  Register #(.width(3)) register_1 (
    .D(comparator_1_gt), .en(CMP), .clk(controlled_buffer_6_out), .Q(register_1_q), .clr(Reset));
  or or_4 (or_4_out, JL, JE, JG, JMP);
  assign controlled_buffer_39_out = or_4_out ? INV_VAL : 1'bz;  // Controlled_Buffer controlled_buffer_39
  and and_4 (and_4_out, JG, register_1_q[0]);
  and and_5 (and_5_out, JE, register_1_q[1]);
  and and_6 (and_6_out, JL, register_1_q[2]);
  or or_5 (or_5_out, and_6_out, and_5_out, and_4_out, JMP);
  xor xor_2 (xor_2_out, or_5_out, controlled_buffer_39_out);
  buf buffer_1 (buffer_1_out, CLOCK3);
  buf buffer_2 (buffer_2_out, buffer_1_out);
  buf buffer_3 (Clock_OU, buffer_2_out);
  Counter #(.max('hffff), .width(16)) counter_1 (
    .clr(Reset), .load(xor_2_out), .clk(controlled_buffer_6_out), .D(OP), .Q(Instruction_Pointer));  // open: up, count, carry
  and and_7 (WRT, WRT_t, CLOCK3);

  // Other names for the same wires on the sheet: CLOCK0 = Clock; SRC1_IMM[15:0] = OP
endmodule

module CPU_Decoder (
  input  [3:0] OPCODE,
  input  UNENABLE,
  output NOOP,
  output MOV,
  output AMD,
  output OW,
  output XOW,
  output ADD,
  output SUB,
  output SHL,
  output SHR,
  output CMP,
  output JMP,
  output JE,
  output JL,
  output JG,
  output WRT,
  output READ,
  output SRC_1,
  output SRC_2,
  output OU
);

  wire not_1_out;
  wire [3:0] and_1_out, controlled_buffer_1_out;

  assign controlled_buffer_1_out = not_1_out ? 4'b1111 : 4'bz;  // Controlled_Buffer controlled_buffer_1
  not not_1 (not_1_out, UNENABLE);
  assign and_1_out = OPCODE & controlled_buffer_1_out;  // AND_Gate and_1, 4 bits wide
  assign controlled_buffer_1_out = UNENABLE ? ~4'b1111 : 4'bz;  // Controlled_Inverter controlled_inverter_1
  Decoder #(.enable("false"), .select(4)) decoder_1 (
    .out0(NOOP), .out1(MOV), .out2(AMD), .out3(OW), .out4(XOW), .out5(ADD), .out6(SUB), .out7(SHL),
    .out8(SHR), .out9(CMP), .out10(JMP), .out11(JE), .out12(JL), .out13(JG), .out14(WRT), .out15(READ),
    .sel(and_1_out));
  nor nor_1 (OU, NOOP, CMP, JMP, JE, JL, JG, WRT);
  nor nor_2 (SRC_1, NOOP, READ, UNENABLE);
  or or_1 (SRC_2, AMD, OW, XOW, WRT, ADD, SUB, CMP, READ);
endmodule

module REG_Decoder (
  input  [2:0] IP,
  input  ENABLE,
  output A,
  output B,
  output C,
  output D,
  output s,
  output t,
  output BP,
  output SP
);

  Demultiplexer #(.select(3)) demultiplexer_1 (
    .out0(A), .out1(B), .out2(C), .out3(D), .out4(s), .out5(t), .out6(BP), .out7(SP), .in(ENABLE), .sel(IP));
endmodule

module Buffering (
  input  in_1,
  output out_2
);

  wire buffer_1_out, buffer_2_out, buffer_3_out, buffer_4_out, buffer_5_out, buffer_6_out, buffer_7_out,
       buffer_8_out, buffer_9_out;

  buf buffer_1 (buffer_1_out, in_1);
  buf buffer_2 (buffer_2_out, buffer_1_out);
  buf buffer_3 (buffer_3_out, buffer_2_out);
  buf buffer_4 (buffer_4_out, buffer_3_out);
  buf buffer_5 (buffer_5_out, buffer_4_out);
  buf buffer_6 (buffer_6_out, buffer_5_out);
  buf buffer_7 (buffer_7_out, buffer_6_out);
  buf buffer_8 (buffer_8_out, buffer_7_out);
  buf buffer_9 (buffer_9_out, buffer_8_out);
  buf buffer_10 (out_2, buffer_9_out);
endmodule

module IMM_SAVE (
  input  IMM_VAL,
  input  [15:0] INSTR_IN,
  input  Clock,
  input  Reset,
  output [15:0] out_5,
  output IMM_ENABLE
);

  wire and_1_out, not_1_out;

  and and_1 (and_1_out, not_1_out, IMM_VAL);
  not not_1 (not_1_out, IMM_ENABLE);
  D_Flip_Flop #(.trigger("falling")) d_ff_1 (
    .D(and_1_out), .clk(Clock), .Q(IMM_ENABLE), .reset(Reset));  // open: Qn, preset
  Register #(.width(16)) register_1 (.D(INSTR_IN), .en(and_1_out), .clk(Clock), .Q(out_5), .clr(Reset));

  // Other names for the same wires on the sheet: IMM_EN = IMM_ENABLE
endmodule

module IMM_SAVE2 (
  input  [1:0] IMM_VALS,
  input  [15:0] INSTR_IN,
  input  Clock,
  input  Reset,
  output [15:0] INSTRUCTION,
  output OPCODE_DISABLE,
  output SRC1_IMM,
  output [15:0] SRC1,
  output SRC2_IMM,
  output [15:0] SRC2
);

  wire and_1_out, and_2_out, and_3_out, and_4_out, decoder_1_out1, decoder_1_out2, decoder_1_out3, IMM_EN3_1,
       IMM_EN3_2, IMM_EN_SRC1, IMM_EN_SRC2, IP_ENABLE, not_1_out, not_2_out, not_3_out, not_4_out, not_5_out,
       or_3_out, or_4_out, or_5_out, SINGLE_IMM, WRT_EN, xor_1_out;

  or or_1 (SINGLE_IMM, IMM_VALS[0], IMM_VALS[1]);
  Decoder #(.select(2)) decoder_1 (
    .out1(decoder_1_out1), .out2(decoder_1_out2), .out3(decoder_1_out3), .sel(IMM_VALS), .en(IP_ENABLE));  // open: out0
  or or_2 (WRT_EN, decoder_1_out3, decoder_1_out2, decoder_1_out1);
  and and_1 (and_1_out, not_2_out, decoder_1_out1);
  and and_2 (and_2_out, not_3_out, decoder_1_out2);
  and and_3 (and_3_out, not_1_out, decoder_1_out3);
  not not_1 (not_1_out, IMM_EN3_1);
  D_Flip_Flop #(.trigger("falling")) d_ff_1 (
    .D(and_3_out), .clk(Clock), .Q(IMM_EN3_1), .reset(Reset));  // open: Qn, preset
  not not_2 (not_2_out, IMM_EN_SRC2);
  D_Flip_Flop #(.trigger("falling")) d_ff_2 (
    .D(and_1_out), .clk(Clock), .Q(IMM_EN_SRC2), .reset(Reset));  // open: Qn, preset
  not not_3 (not_3_out, IMM_EN_SRC1);
  D_Flip_Flop #(.trigger("falling")) d_ff_3 (
    .D(and_2_out), .clk(Clock), .Q(IMM_EN_SRC1), .reset(Reset));  // open: Qn, preset
  and and_4 (and_4_out, not_4_out, IMM_EN3_1);
  Register #(.width(16)) register_1 (.D(INSTR_IN), .en(WRT_EN), .clk(Clock), .Q(INSTRUCTION), .clr(Reset));
  not not_4 (not_4_out, IMM_EN3_2);
  D_Flip_Flop #(.trigger("falling")) d_ff_4 (
    .D(and_4_out), .clk(Clock), .Q(IMM_EN3_2), .reset(Reset));  // open: Qn, preset
  or or_3 (or_3_out, IMM_EN_SRC1, IMM_EN3_1);
  or or_4 (or_4_out, IMM_EN_SRC2, IMM_EN3_2);
  Register #(.width(16)) register_2 (.D(INSTR_IN), .en(or_3_out), .clk(Clock), .Q(SRC1), .clr(Reset));
  Register #(.width(16)) register_3 (.D(INSTR_IN), .en(or_4_out), .clk(Clock), .Q(SRC2), .clr(Reset));
  or or_5 (or_5_out, IMM_EN_SRC1, IMM_EN_SRC2, IMM_EN3_2);
  not not_5 (not_5_out, or_5_out);
  xor xor_1 (xor_1_out, SINGLE_IMM, or_5_out);
  xor xor_2 (IP_ENABLE, not_5_out, IMM_EN3_1);
  or or_6 (OPCODE_DISABLE, xor_1_out, IMM_EN3_1);
  or or_7 (OPCODE_DISABLE, xor_1_out, IMM_EN3_1);
  or or_8 (SRC1_IMM, IMM_EN3_2, IMM_EN_SRC1);
  or or_9 (SRC2_IMM, IMM_EN3_2, IMM_EN_SRC2);

  // Other names for the same wires on the sheet: INSTR[15:0] = INSTRUCTION
endmodule
